# Fritzing sketch Ejemplo-1 (saved by Fritzing 0.9.3b)
breadboards: 1

parts:
  Part2 = iceZUM Alhambra
  LED1 = LED - 5mm [color="Red (633nm)" package="5 mm [THT]"]
  R1 = Resistor [tolerance=±5% resistance=100 package="0603 [SMD]"]

nets:
  N1: Part2.GP0, LED1.anode
  N2: Part2.GND, R1.Pin_1
  N3: LED1.cathode, R1.Pin_0

custom parts:
  iceZUM Alhambra: Arduino/zum compatible Open FPGA electronic board. Synthesize hardware easily, using only open source tools
