# Fritzing sketch Ejemplo-2 (saved by Fritzing 0.9.3b)
breadboards: 1

parts:
  LED1 = LED - 5mm [color="Red (633nm)" package="5 mm [THT]"]
  R1 = Resistor [tolerance=±5% resistance=100 package="0603 [SMD]"]
  Part3 = iceZUM Alhambra
  R2 = Resistor [tolerance=±5% resistance=100 package="0603 [SMD]"]
  LED2 = LED - 5mm [color="Red (633nm)" package="5 mm [THT]"]

nets:
  N1: LED1.cathode, R1.Pin_0
  N2: LED1.anode, Part3.GP0
  N3: R1.Pin_1, Part3.GD3, Part3.GND, R2.Pin_1
  N4: Part3.GP7, LED2.anode
  N5: R2.Pin_0, LED2.cathode

custom parts:
  iceZUM Alhambra: Arduino/zum compatible Open FPGA electronic board. Synthesize hardware easily, using only open source tools
