# Fritzing sketch Interruptor-3v3-breadboard (saved by Fritzing 0.9.3b)
breadboards: 1

parts:
  Part1 = iceZUM Alhambra
  U1 = SWITCH_SPDT [package=kps-1290]

nets:
  N1: Part1.GD5, U1.S
  N2: Part1.GP0, U1.P
  N3: Part1.3V3, U1.O

custom parts:
  iceZUM Alhambra: Arduino/zum compatible Open FPGA electronic board. Synthesize hardware easily, using only open source tools
