# Fritzing sketch Esquema-1-LED-protoboard (saved by Fritzing 0.9.3b)
breadboards: 1

parts:
  LED1 = LED - 5mm [color="Red (633nm)" package="5 mm [THT]"]
  Part3 = iceZUM Alhambra
  R1 = Resistor [tolerance=±5% resistance=220 package=THT]
  Q1 = TRANSISTOR_PNP [package=to-92]
  R2 = Resistor [tolerance=±5% resistance=10k package=THT]

nets:
  N1: LED1.cathode, R1.Pin_0
  N2: LED1.anode, Part3.V13#32
  N3: Part3.G13, Q1.C
  N4: Part3.V13#46, R2.Pin_1
  N5: R1.Pin_1, Q1.E
  N6: Q1.B, R2.Pin_0

custom parts:
  iceZUM Alhambra: Arduino/zum compatible Open FPGA electronic board. Synthesize hardware easily, using only open source tools
