# Fritzing sketch Esquema-2-Buzzer-protoboard (saved by Fritzing 0.9.3b)
breadboards: 1

parts:
  Part3 = iceZUM Alhambra
  Q1 = TRANSISTOR_PNP [package=to-92]
  R2 = Resistor [tolerance=±5% resistance=10k package=THT]
  J1 = Piezo Speaker

nets:
  N1: Part3.G13, Q1.C
  N2: Part3.V13#32, J1.pin2
  N3: Part3.V13#46, R2.Pin_1
  N4: Q1.E, J1.pin1
  N5: Q1.B, R2.Pin_0

custom parts:
  iceZUM Alhambra: Arduino/zum compatible Open FPGA electronic board. Synthesize hardware easily, using only open source tools
