# Fritzing sketch arduino-alhambra-2 (saved by Fritzing 0.9.3b)

parts:
  Part1 = iceZUM Alhambra
  Part2 = Arduino Uno (Rev3) - ICSP

nets:
  N1: Part1.D9, Part2.D9_PWM
  N2: Part1.D10, Part2.D10_PWM/SS
  N3: Part1.D12, Part2.D12/MISO
  N4: Part1.G, Part1.G5, Part2.GND

custom parts:
  iceZUM Alhambra: Arduino/zum compatible Open FPGA electronic board. Synthesize hardware easily, using only open source tools
