# Fritzing sketch Alhambra-hc-05 (saved by Fritzing 0.9.3b)

parts:
  Part1 = Bluetooth HC-05 Macho
  Part2 = iceZUM Alhambra

nets:
  N1: Part1.TXD, Part2.GP0
  N2: Part1.RXD, Part2.GP1
  N3: Part1.VCC, Part2.VD5
  N4: Part1.GND, Part2.GD5

custom parts:
  iceZUM Alhambra: Arduino/zum compatible Open FPGA electronic board. Synthesize hardware easily, using only open source tools
